# Fritzing sketch ESP32C3-GPS (saved by Fritzing 1.0.5)
breadboards: 1

parts:
  A1 = lolin C3 mini
  A2 = NEO-6M GPS Module [part_number=GY-GPS6MV2]

nets:
  N1: A1.Pin_9, A2.Vcc
  N2: A1.Pin_15, A2.Tx

custom parts:
  lolin C3 mini: WiFi + Bluetooth 5 (LE) boards based ESP32-C3FH4.
  NEO-6M GPS Module: GY-GPS6MV2 NEO-6M GPS Module Module based on U-blox NEO-6M GPS engine, incorporating regulator for 3.3-5V DC input, MS621FE-compatible rechargeable battery for backup and EEPROM for storing configuration settings. Links: NEO-6 series product information page NEO-6 Datasheet
