# Fritzing sketch MAX30102 (saved by Fritzing 1.0.5)
breadboards: 1

parts:
  A1 = XIAO ESP32C3-smd
  M1 = NEO-6M GPS Module [part_number=GY-GPS6MV2]
  M2 = MakerFocus MAX30102  # not connected

nets:
  N1: A1.Pin_2, A1.Pin_21, M1.GND
  N2: A1.Pin_16, M1.Rx
  N3: A1.Pin_22, M1.Vcc

custom parts:
  XIAO ESP32C3-smd: Seeed Studio XIAO ESP32C3 adopts new RISC-V architecture, supporting both Wi-Fi and BLE wireless connectivities.
  NEO-6M GPS Module: GY-GPS6MV2 NEO-6M GPS Module Module based on U-blox NEO-6M GPS engine, incorporating regulator for 3.3-5V DC input, MS621FE-compatible rechargeable battery for backup and EEPROM for storing configuration settings. Links: NEO-6 series product information page NEO-6 Datasheet
  MakerFocus MAX30102: Oximeter module using the MAX30102 chip. As usual, if you want the mounting holes in pcb, you need to drag a hole over the pad in silkscreen to actually drill the hole (by default they are not drilled)
