# Fritzing sketch SetupGPS (saved by Fritzing 1.0.5)
breadboards: 1

parts:
  A1 = seeed-XIAO_ESP32C3-smd_1
  M1 = NEO-6M GPS Module [part_number=GY-GPS6MV2]

nets:
  N1: A1.connector15, M1.Rx
  N2: A1.connector20, M1.GND
  N3: A1.connector21, M1.Vcc

custom parts:
  NEO-6M GPS Module: GY-GPS6MV2 NEO-6M GPS Module Module based on U-blox NEO-6M GPS engine, incorporating regulator for 3.3-5V DC input, MS621FE-compatible rechargeable battery for backup and EEPROM for storing configuration settings. Links: NEO-6 series product information page NEO-6 Datasheet
