# Fritzing sketch HX-711 (saved by Fritzing 1.0.5)
breadboards: 1

parts:
  A1 = XIAO ESP32C3-smd
  M1 = NEO-6M GPS Module [part_number=GY-GPS6MV2]
  Part1 = HX711 Weighing Sensor Module
  Load_Cell1 = Load Cell - Red/white/black/green

nets:
  GND: A1.Pin_2, A1.Pin_21, M1.GND, Part1.GND
  N1: A1.Pin_10, Part1.DO/RX
  N2: A1.Pin_11, Part1.CK/TX
  N3: A1.Pin_16, M1.Tx
  N4: A1.Pin_20, Part1.VCC
  N5: Part1.E+, Load_Cell1.wire1
  N6: Part1.E-, Load_Cell1.wire3
  N7: Part1.A+, Load_Cell1.wire2
  N8: Part1.A-, Load_Cell1.wire4

notes:
  Weight
  Obs. Prop id: 28
  Datastream id:
  HX-711
  Sensor id: 20
  Thing id:
  Thing name:
  UoM:
  gram

custom parts:
  XIAO ESP32C3-smd: Seeed Studio XIAO ESP32C3 adopts new RISC-V architecture, supporting both Wi-Fi and BLE wireless connectivities.
  NEO-6M GPS Module: GY-GPS6MV2 NEO-6M GPS Module Module based on U-blox NEO-6M GPS engine, incorporating regulator for 3.3-5V DC input, MS621FE-compatible rechargeable battery for backup and EEPROM for storing configuration settings. Links: NEO-6 series product information page NEO-6 Datasheet
  HX711 Weighing Sensor Module: HX711 is a precision 24-bit analog-to-digital converter (ADC) designed for weigh scales and industrial control applications to interface directly with a bridge sensor.
  Load Cell - Red/white/black/green: A rectangle load cell/weighting pressure Sensor with four wires - Red, white, black, green. Normally corresponding with E+, E-, A+, A- respectively.
