# Fritzing sketch MAX4466 (saved by Fritzing 1.0.5)
breadboards: 1

parts:
  A1 = seeed-XIAO_ESP32C3-smd_1
  M1 = NEO-6M GPS Module [part_number=GY-GPS6MV2]
  Part1 = Adafruit MAX4466 Electret Microphone Amplifier [part_number="Adafruit #1063"]

nets:
  N1: A1.connector15, M1.Rx
  N2: A1.connector19, Part1.VCC
  GND: A1.connector20, M1.GND, Part1.GND
  N3: A1.connector21, M1.Vcc

custom parts:
  NEO-6M GPS Module: GY-GPS6MV2 NEO-6M GPS Module Module based on U-blox NEO-6M GPS engine, incorporating regulator for 3.3-5V DC input, MS621FE-compatible rechargeable battery for backup and EEPROM for storing configuration settings. Links: NEO-6 series product information page NEO-6 Datasheet
  Adafruit MAX4466 Electret Microphone Amplifier: Add an ear to your project with this well-designed electret microphone amplifier. This fully assembled and tested board comes with a 20-20KHz electret microphone soldered on. For the amplification, we use the Maxim MAX4466, an op-amp specifically designed for this delicate task! The amplifier has excellent power supply noise rejection, so this amplifier sounds really good and isn't nearly as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
