# Fritzing sketch MH_ET_Live (saved by Fritzing 1.0.5)
breadboards: 1

parts:
  A1 = lolin C3 mini
  A2 = NEO-6M GPS Module [part_number=GY-GPS6MV2]
  A3 = fc-51 [package=THT]

nets:
  N1: A1.Pin_9, A2.Vcc
  N2: A1.Pin_15, A2.Tx
  N3: A3.Pin_4, A3.Pin_8

custom parts:
  lolin C3 mini: WiFi + Bluetooth 5 (LE) boards based ESP32-C3FH4.
  NEO-6M GPS Module: GY-GPS6MV2 NEO-6M GPS Module Module based on U-blox NEO-6M GPS engine, incorporating regulator for 3.3-5V DC input, MS621FE-compatible rechargeable battery for backup and EEPROM for storing configuration settings. Links: NEO-6 series product information page NEO-6 Datasheet
  fc-51: Fc-51 Infrared Obstacle Avoidance Proximity Sensor module. IR transmitter led, receiver LED, lm393 compaitor and a pot. 3.3 V to 5V power.
