# Fritzing sketch HMC5883L (saved by Fritzing 1.0.5)
breadboards: 1

parts:
  A1 = seeed-XIAO_ESP32C3-smd_1
  M1 = NEO-6M GPS Module [part_number=GY-GPS6MV2]
  Part1 = HMC5883L Triple-axis Magnetometer [part_number=1746]

nets:
  N1: A1.connector15, M1.Rx
  N2: A1.connector19, Part1.VIN
  GND: A1.connector20, M1.GND, Part1.GND
  N3: A1.connector21, M1.Vcc

custom parts:
  NEO-6M GPS Module: GY-GPS6MV2 NEO-6M GPS Module Module based on U-blox NEO-6M GPS engine, incorporating regulator for 3.3-5V DC input, MS621FE-compatible rechargeable battery for backup and EEPROM for storing configuration settings. Links: NEO-6 series product information page NEO-6 Datasheet
  HMC5883L Triple-axis Magnetometer: A magnetometer can sense where the strongest magnetic force is coming from, generally used to detect magnetic north. We based this breakout on a popular and well loved magnetometer, the HMC5883L. This compact sensor uses I2C to communicate and its very easy to use. Since it's a 3.3V max chip, we added circuitry to make it 5V-safe logic and power, for easy use with either 3 or 5V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
