# Fritzing sketch HX711 (saved by Fritzing 1.0.5)
breadboards: 1

parts:
  A1 = seeed-XIAO_ESP32C3-smd_1
  M1 = NEO-6M GPS Module [part_number=GY-GPS6MV2]
  Part1 = HX711 Weighing Sensor Module
  Load_Cell1 = Load Cell - Red/white/black/green

nets:
  N1: A1.connector15, M1.Rx
  N2: A1.connector19, Part1.VCC
  GND: A1.connector20, M1.GND, Part1.GND
  N3: A1.connector21, M1.Vcc
  N4: Part1.E+, Load_Cell1.wire1
  N5: Part1.E-, Load_Cell1.wire3
  N6: Part1.A+, Load_Cell1.wire2
  N7: Part1.A-, Load_Cell1.wire4

custom parts:
  NEO-6M GPS Module: GY-GPS6MV2 NEO-6M GPS Module Module based on U-blox NEO-6M GPS engine, incorporating regulator for 3.3-5V DC input, MS621FE-compatible rechargeable battery for backup and EEPROM for storing configuration settings. Links: NEO-6 series product information page NEO-6 Datasheet
  HX711 Weighing Sensor Module: HX711 is a precision 24-bit analog-to-digital converter (ADC) designed for weigh scales and industrial control applications to interface directly with a bridge sensor.
  Load Cell - Red/white/black/green: A rectangle load cell/weighting pressure Sensor with four wires - Red, white, black, green. Normally corresponding with E+, E-, A+, A- respectively.
